# Fritzing sketch eeg_lucid_dream (saved by Fritzing 0.9.4)
breadboards: 1

parts:
  Part1 = Arduino Uno (Rev3)
  LCD1 = LCD screen
  U1 = Optocoupler [package=THT]
  R1 = Resistor [tolerance=±5% resistance=220 package=THT]
  J1 = Piezo Speaker

nets:
  N1: Part1.D8, J1.pin2
  N2: Part1.D11_PWM/MOSI, LCD1.E
  N3: Part1.D12/MISO, LCD1.RS
  GND: Part1.GND, LCD1.VSS, LCD1.R/W, LCD1.LED-, J1.pin1
  N4: Part1.D0/RX, U1.Pin_4
  N5: Part1.D1/TX, U1.Pin_6
  N6: Part1.D2, LCD1.DB7
  N7: Part1.D3_PWM, LCD1.DB6
  N8: Part1.D4, LCD1.DB5
  N9: Part1.D5_PWM, LCD1.DB4
  5V: Part1.5V, LCD1.VDD, R1.Pin_0
  N10: LCD1.LED+, R1.Pin_1
